// Logisim project ALU and RB.circ as structural Verilog: 3 circuits, main circuit ULA
module ULA (
  input  [31:0] A,
  input  [31:0] B,
  input  [3:0] OP,
  input  [4:0] Shamt,
  output [31:0] Result,
  output Zero,
  output Overflow
);

  wire add, adder_1_cout, and_2_out, and_6_out, and_7_out, and_8_out, and_9_out, and_10_out, and_11_out,
       and_13_out, and_14_out, comparator_2_gt, comparator_3_gt, comparator_4_lt, comparator_5_lt,
       comparator_6_gt, comparator_7_lt, comparator_8_lt, comparator_9_gt, comparator_10_lt,
       comparator_11_gt, comparator_12_gt, comparator_13_gt, OvA, OvA_minus, OvA_plus, OvS, OvS_minus,
       OvS_plus, sub, subtractor_1_bout;
  wire [0:0] comparator_1_lt;
  wire [31:0] addRes, and_1_out, nor_1_out, or_1_out, shifter_1_out, shifter_2_out, subtractor_1_out,
       xor_1_out;

  assign and_1_out = A & B;  // AND_Gate and_1, 32 bits wide
  assign or_1_out = A | B;  // OR_Gate or_1, 32 bits wide
  Adder #(.width(32)) adder_1 (.a(A), .b(B), .out(addRes), .cout(adder_1_cout));  // open: cin
  and and_2 (and_2_out, adder_1_cout, add);
  assign xor_1_out = A ^ B;  // XOR_Gate xor_1, 32 bits wide
  Shifter #(.width(32)) shifter_1 (.in(B), .\dist (Shamt), .out(shifter_1_out));
  Shifter #(.width(32), .shift("lr")) shifter_2 (.in(B), .\dist (Shamt), .out(shifter_2_out));
  Subtractor #(.width(32)) subtractor_1 (.a(A), .b(B), .out(subtractor_1_out), .bout(subtractor_1_bout));  // open: bin
  // AND_Gate and_3 has open pins: in0=subtractor_1_bout, in1=sub, out=open
  Comparator #(.width(32)) comparator_1 (.a(A), .b(B), .lt(comparator_1_lt[0]));  // open: gt, eq
  assign nor_1_out = ~(A | B);  // NOR_Gate nor_1, 32 bits wide
  or or_2 (OvA, and_2_out, OvA_plus, OvA_minus);
  or or_3 (OvS, OvS_plus, OvS_minus);
  Multiplexer #(.select(4), .width(32), .enable("false")) multiplexer_1 (
    .in0(and_1_out), .in1(or_1_out), .in2(addRes), .in3(xor_1_out), .in4(shifter_1_out), .in5(shifter_2_out),
    .in6(subtractor_1_out), .in7({{31{1'b0}}, comparator_1_lt[0]}), .in12(nor_1_out), .out(Result), .sel(OP));  // open: in8, in9, in10, in11, in13, in14, in15
  and and_4 (add, ~OP[3], ~OP[2], OP[1], ~OP[0]);  // AND_Gate
  and and_5 (sub, ~OP[3], OP[2], OP[1], ~OP[0]);  // AND_Gate
  nor nor_2 (Zero, Result[31], Result[30], Result[29], Result[28], Result[27], Result[26], Result[25], Result[24], Result[23], Result[22], Result[21], Result[20], Result[19], Result[18], Result[17], Result[16], Result[15], Result[14], Result[13], Result[12], Result[11], Result[10], Result[9], Result[8], Result[7], Result[6], Result[5], Result[4], Result[3], Result[2], Result[1], Result[0]);
  Comparator #(.width(32), .mode("unsigned")) comparator_2 (
    .a(A), .b({32{1'b0}}), .gt(comparator_2_gt));  // open: eq, lt
  Comparator #(.width(32), .mode("unsigned")) comparator_3 (
    .a(B), .b({32{1'b0}}), .gt(comparator_3_gt));  // open: eq, lt
  Comparator #(.width(32), .mode("unsigned")) comparator_4 (
    .a(A), .b({32{1'b0}}), .lt(comparator_4_lt));  // open: gt, eq
  Comparator #(.width(32), .mode("unsigned")) comparator_5 (
    .a(B), .b({32{1'b0}}), .lt(comparator_5_lt));  // open: gt, eq
  Comparator #(.width(32), .mode("unsigned")) comparator_6 (
    .a(A), .b({32{1'b0}}), .gt(comparator_6_gt));  // open: eq, lt
  Comparator #(.width(32), .mode("unsigned")) comparator_7 (
    .a(B), .b({32{1'b0}}), .lt(comparator_7_lt));  // open: gt, eq
  Comparator #(.width(32), .mode("unsigned")) comparator_8 (
    .a(A), .b({32{1'b0}}), .lt(comparator_8_lt));  // open: gt, eq
  Comparator #(.width(32), .mode("unsigned")) comparator_9 (
    .a(B), .b({32{1'b0}}), .gt(comparator_9_gt));  // open: eq, lt
  or or_4 (Overflow, OvA, OvS);
  and and_6 (and_6_out, comparator_2_gt, comparator_3_gt);
  Comparator #(.width(32)) comparator_10 (.a(addRes), .b({32{1'b0}}), .lt(comparator_10_lt));  // open: gt, eq
  and and_7 (and_7_out, comparator_4_lt, comparator_5_lt);
  Comparator #(.width(32)) comparator_11 (.a(addRes), .b({32{1'b0}}), .gt(comparator_11_gt));  // open: eq, lt
  and and_8 (and_8_out, comparator_6_gt, comparator_7_lt);
  Comparator #(.width(32)) comparator_12 (.a(addRes), .b({32{1'b0}}), .gt(comparator_12_gt));  // open: eq, lt
  and and_9 (and_9_out, comparator_8_lt, comparator_9_gt);
  Comparator #(.width(32)) comparator_13 (.a(addRes), .b({32{1'b0}}), .gt(comparator_13_gt));  // open: eq, lt
  and and_10 (and_10_out, and_6_out, comparator_10_lt);
  and and_11 (and_11_out, and_7_out, comparator_11_gt);
  and and_12 (OvS_plus, sub, and_13_out);
  and and_13 (and_13_out, and_8_out, comparator_12_gt);
  and and_14 (and_14_out, and_9_out, comparator_13_gt);
  and and_15 (OvA_plus, add, and_10_out);
  and and_16 (OvA_minus, add, and_11_out);
  and and_17 (OvS_minus, sub, and_14_out);

  // Notes on the sheet:
  //   Overflow para Subtração
  //   Overflow para Adição
  //   AND 0000
  //   OR 0001
  //   ADD 0010
  //   XOR 0011
  //   SLL 0100
  //   SLR 0101
  //   SUB 0110
  //   SLT 0111
  //   NOR 1100
endmodule

// Register Bank
module Banco_de_Registradores_de_32_bits (
  input  RegWrite,
  input  [4:0] WR,
  input  [31:0] WD,
  input  Clear,
  input  Clock,
  input  [4:0] LR1,
  input  [4:0] LR2,
  output [31:0] LD1,
  output [31:0] LD2
);

  wire demultiplexer_1_out0, demultiplexer_1_out1, demultiplexer_1_out2, demultiplexer_1_out3,
       demultiplexer_1_out4, demultiplexer_1_out5, demultiplexer_1_out6, demultiplexer_1_out7,
       demultiplexer_1_out8, demultiplexer_1_out9, demultiplexer_1_out10, demultiplexer_1_out11,
       demultiplexer_1_out12, demultiplexer_1_out13, demultiplexer_1_out14, demultiplexer_1_out15,
       demultiplexer_1_out16, demultiplexer_1_out17, demultiplexer_1_out18, demultiplexer_1_out19,
       demultiplexer_1_out20, demultiplexer_1_out21, demultiplexer_1_out22, demultiplexer_1_out23,
       demultiplexer_1_out24, demultiplexer_1_out25, demultiplexer_1_out26, demultiplexer_1_out27,
       demultiplexer_1_out28, demultiplexer_1_out29, demultiplexer_1_out30, demultiplexer_1_out31;
  wire [31:0] _0_q, a0_q, a1_q, a2_q, a3_q, at_q, fp_q, gp_q, k0_q, k1_q, ra_q, s0_q, s1_q, s2_q, s3_q, s4_q,
       s5_q, s6_q, s7_q, sp_q, t0_q, t1_q, t2_q, t3_q, t4_q, t5_q, t6_q, t7_q, t8_q, t9_q, v0_q, v1_q;

  Demultiplexer #(.select(5), .enable("false")) demultiplexer_1 (
    .out0(demultiplexer_1_out0), .out1(demultiplexer_1_out1), .out2(demultiplexer_1_out2),
    .out3(demultiplexer_1_out3), .out4(demultiplexer_1_out4), .out5(demultiplexer_1_out5),
    .out6(demultiplexer_1_out6), .out7(demultiplexer_1_out7), .out8(demultiplexer_1_out8),
    .out9(demultiplexer_1_out9), .out10(demultiplexer_1_out10), .out11(demultiplexer_1_out11),
    .out12(demultiplexer_1_out12), .out13(demultiplexer_1_out13), .out14(demultiplexer_1_out14),
    .out15(demultiplexer_1_out15), .out16(demultiplexer_1_out16), .out17(demultiplexer_1_out17),
    .out18(demultiplexer_1_out18), .out19(demultiplexer_1_out19), .out20(demultiplexer_1_out20),
    .out21(demultiplexer_1_out21), .out22(demultiplexer_1_out22), .out23(demultiplexer_1_out23),
    .out24(demultiplexer_1_out24), .out25(demultiplexer_1_out25), .out26(demultiplexer_1_out26),
    .out27(demultiplexer_1_out27), .out28(demultiplexer_1_out28), .out29(demultiplexer_1_out29),
    .out30(demultiplexer_1_out30), .out31(demultiplexer_1_out31), .in(RegWrite), .sel(WR));
  Register #(.width(32)) _0 (.D({32{1'b0}}), .Q(_0_q));  // open: en, clk, clr
  Register #(.width(32)) at (.D(WD), .en(demultiplexer_1_out1), .Q(at_q), .clk(Clock), .clr(Clear));
  Register #(.width(32)) v0 (.D(WD), .en(demultiplexer_1_out2), .Q(v0_q), .clk(Clock), .clr(Clear));
  Register #(.width(32)) v1 (.D(WD), .en(demultiplexer_1_out3), .Q(v1_q), .clk(Clock), .clr(Clear));
  Register #(.width(32)) a0 (.D(WD), .en(demultiplexer_1_out4), .Q(a0_q), .clk(Clock), .clr(Clear));
  Register #(.width(32)) a1 (.D(WD), .en(demultiplexer_1_out5), .Q(a1_q), .clk(Clock), .clr(Clear));
  Register #(.width(32)) a2 (.D(WD), .en(demultiplexer_1_out6), .Q(a2_q), .clk(Clock), .clr(Clear));
  Register #(.width(32)) a3 (.D(WD), .en(demultiplexer_1_out7), .Q(a3_q), .clk(Clock), .clr(Clear));
  Register #(.width(32)) t0 (.D(WD), .en(demultiplexer_1_out8), .Q(t0_q), .clk(Clock), .clr(Clear));
  Register #(.width(32)) t1 (.D(WD), .en(demultiplexer_1_out9), .Q(t1_q), .clk(Clock), .clr(Clear));
  Register #(.width(32)) t2 (.D(WD), .en(demultiplexer_1_out10), .Q(t2_q), .clk(Clock), .clr(Clear));
  Register #(.width(32)) t3 (.D(WD), .en(demultiplexer_1_out11), .Q(t3_q), .clk(Clock), .clr(Clear));
  Register #(.width(32)) t4 (.D(WD), .en(demultiplexer_1_out12), .Q(t4_q), .clk(Clock), .clr(Clear));
  Register #(.width(32)) t5 (.D(WD), .en(demultiplexer_1_out13), .Q(t5_q), .clk(Clock), .clr(Clear));
  Register #(.width(32)) t6 (.D(WD), .en(demultiplexer_1_out14), .Q(t6_q), .clk(Clock), .clr(Clear));
  Register #(.width(32)) t7 (.D(WD), .en(demultiplexer_1_out15), .Q(t7_q), .clk(Clock), .clr(Clear));
  Register #(.width(32)) s0 (.D(WD), .en(demultiplexer_1_out16), .Q(s0_q), .clk(Clock), .clr(Clear));
  Register #(.width(32)) s2 (.D(WD), .en(demultiplexer_1_out18), .Q(s2_q), .clk(Clock), .clr(Clear));
  Register #(.width(32)) s1 (.D(WD), .en(demultiplexer_1_out17), .Q(s1_q), .clk(Clock), .clr(Clear));
  Register #(.width(32)) s3 (.D(WD), .en(demultiplexer_1_out19), .Q(s3_q), .clk(Clock), .clr(Clear));
  Register #(.width(32)) s4 (.D(WD), .en(demultiplexer_1_out20), .Q(s4_q), .clk(Clock), .clr(Clear));
  Register #(.width(32)) s6 (.D(WD), .en(demultiplexer_1_out22), .Q(s6_q), .clk(Clock), .clr(Clear));
  Register #(.width(32)) s5 (.D(WD), .en(demultiplexer_1_out21), .Q(s5_q), .clk(Clock), .clr(Clear));
  Register #(.width(32)) s7 (.D(WD), .en(demultiplexer_1_out23), .Q(s7_q), .clk(Clock), .clr(Clear));
  Register #(.width(32)) t8 (.D(WD), .en(demultiplexer_1_out24), .Q(t8_q), .clk(Clock), .clr(Clear));
  Register #(.width(32)) t9 (.D(WD), .en(demultiplexer_1_out25), .Q(t9_q), .clk(Clock), .clr(Clear));
  Register #(.width(32)) k0 (.D(WD), .en(demultiplexer_1_out26), .Q(k0_q), .clk(Clock), .clr(Clear));
  Register #(.width(32)) k1 (.D(WD), .en(demultiplexer_1_out27), .Q(k1_q), .clk(Clock), .clr(Clear));
  Register #(.width(32)) gp (.D(WD), .en(demultiplexer_1_out28), .Q(gp_q), .clk(Clock), .clr(Clear));
  Register #(.width(32)) sp (.D(WD), .en(demultiplexer_1_out29), .Q(sp_q), .clk(Clock), .clr(Clear));
  Register #(.width(32)) fp (.D(WD), .en(demultiplexer_1_out30), .Q(fp_q), .clk(Clock), .clr(Clear));
  Register #(.width(32)) ra (.D(WD), .en(demultiplexer_1_out31), .Q(ra_q), .clk(Clock), .clr(Clear));
  Multiplexer #(.select(5), .width(32), .enable("false")) multiplexer_1 (
    .in0(_0_q), .in1(at_q), .in2(v0_q), .in3(v1_q), .in4(a0_q), .in5(a1_q), .in6(a2_q), .in7(a3_q),
    .in8(t0_q), .in9(t1_q), .in10(t2_q), .in11(t3_q), .in12(t4_q), .in13(t5_q), .in14(t6_q), .in15(t7_q),
    .in16(s0_q), .in17(s1_q), .in18(s2_q), .in19(s3_q), .in20(s4_q), .in21(s5_q), .in22(s6_q), .in23(s7_q),
    .in24(t8_q), .in25(t9_q), .in26(k0_q), .in27(k1_q), .in28(gp_q), .in29(sp_q), .in30(fp_q), .in31(ra_q),
    .out(LD1), .sel(LR1));
  Multiplexer #(.select(5), .width(32), .enable("false")) multiplexer_2 (
    .in0(_0_q), .in1(at_q), .in2(v0_q), .in3(v1_q), .in4(a0_q), .in5(a1_q), .in6(a2_q), .in7(a3_q),
    .in8(t0_q), .in9(t1_q), .in10(t2_q), .in11(t3_q), .in12(t4_q), .in13(t5_q), .in14(t6_q), .in15(t7_q),
    .in16(s0_q), .in17(s1_q), .in18(s2_q), .in19(s3_q), .in20(s4_q), .in21(s5_q), .in22(s6_q), .in23(s7_q),
    .in24(t8_q), .in25(t9_q), .in26(k0_q), .in27(k1_q), .in28(gp_q), .in29(sp_q), .in30(fp_q), .in31(ra_q),
    .out(LD2), .sel(LR2));
endmodule

module MAIN (
);

  ULA ula_1 ();  // open: A, B, Result, OP, Shamt, Zero, Overflow
endmodule
