// Logisim project CU e ALUControl e ECU.circ as structural Verilog: 3 circuits, main circuit UC
module UC (
  input  [5:0] Opcode,
  output AluSrc,
  output RegDst,
  output WriteReg,
  output lui,
  output MemToReg,
  output ExcOut,
  output MTC0,
  output MFC0,
  output MemRead,
  output MemWrite,
  output Branch,
  output \unsigned ,
  output Bne,
  output Link,
  output Jump,
  output [1:0] AluOp
);

  wire addi_out, beq_out, J_out, lw_out, or_1_out, or_6_out;
  wire [1:0] or_8_out;

  and R (RegDst, ~Opcode[0], ~Opcode[1], ~Opcode[2], ~Opcode[3], ~Opcode[4], ~Opcode[5]);  // AND_Gate
  and RFE (ExcOut, ~Opcode[0], ~Opcode[1], ~Opcode[2], ~Opcode[3], ~Opcode[4], Opcode[5]);  // AND_Gate
  and u_mtc0 (MTC0, Opcode[0], ~Opcode[1], ~Opcode[2], ~Opcode[3], ~Opcode[4], Opcode[5]);  // AND_Gate
  and u_mfc0 (MFC0, ~Opcode[0], Opcode[1], ~Opcode[2], ~Opcode[3], ~Opcode[4], Opcode[5]);  // AND_Gate
  and addi (addi_out, ~Opcode[0], ~Opcode[1], ~Opcode[2], Opcode[3], ~Opcode[4], ~Opcode[5]);  // AND_Gate
  and lw (lw_out, Opcode[0], Opcode[1], ~Opcode[2], ~Opcode[3], ~Opcode[4], Opcode[5]);  // AND_Gate
  and sw (MemWrite, Opcode[0], Opcode[1], ~Opcode[2], Opcode[3], ~Opcode[4], Opcode[5]);  // AND_Gate
  and beq (beq_out, ~Opcode[0], ~Opcode[1], Opcode[2], ~Opcode[3], ~Opcode[4], ~Opcode[5]);  // AND_Gate
  and u_bne (Bne, Opcode[0], ~Opcode[1], Opcode[2], ~Opcode[3], ~Opcode[4], ~Opcode[5]);  // AND_Gate
  and u_lui (lui, Opcode[0], Opcode[1], Opcode[2], Opcode[3], ~Opcode[4], ~Opcode[5]);  // AND_Gate
  and ori (\unsigned , Opcode[0], ~Opcode[1], Opcode[2], Opcode[3], ~Opcode[4], ~Opcode[5]);  // AND_Gate
  and J (J_out, ~Opcode[0], Opcode[1], ~Opcode[2], ~Opcode[3], ~Opcode[4], ~Opcode[5]);  // AND_Gate
  and JAL (Link, Opcode[0], Opcode[1], ~Opcode[2], ~Opcode[3], ~Opcode[4], ~Opcode[5]);  // AND_Gate
  or or_1 (or_1_out, lui, \unsigned );
  buf or_2 (MemToReg, lw_out);  // OR_Gate
  buf or_3 (MemRead, lw_out);  // OR_Gate
  or or_4 (AluSrc, addi_out, lw_out, MemWrite, or_1_out);
  or or_5 (Branch, beq_out, Bne);
  or or_6 (or_6_out, ExcOut, \unsigned );
  or or_7 (Jump, J_out, Link);
  or or_8 (or_8_out[0], addi_out, \unsigned , MemWrite, lw_out);
  or or_9 (or_8_out[1], beq_out, \unsigned , Bne);
  or or_10 (WriteReg, RegDst, addi_out, Link, lui, MFC0, lw_out, or_6_out);
  Multiplexer #(.select(3), .width(2), .enable("false")) multiplexer_1 (
    .in0(2'b00), .in1(2'b01), .in2(2'b10), .in3(2'b11), .out(AluOp), .sel({1'b0, or_8_out}));  // open: in4, in5, in6, in7

  // Notes on the sheet:
  //   // Formato I
  //   // Instruções tipo J
  //   000000
  //   100000
  //   100001
  //   100010
  //   001000
  //   100011
  //   101011
  //   000100
  //   000101
  //   001111
  //   001101
  //   000010
  //   000011
endmodule

module ALUControl (
  input  [5:0] Funct,
  input  [1:0] ALUOP,
  output [3:0] OP,
  output Jump_Register
);

  wire [3:0] ADD_out, AND_out, NOR_out, not_1_out, not_5_out, not_8_out, not_11_out, not_15_out, not_18_out,
       or_2_out, OR_out, SLL_out, SLT_out, SRL_out, SUB_out, XOR_out;
  wire [3:1] not_13_out, not_21_out;
  wire [3:2] not_17_out;
  wire [3:3] _100100_out;

  and _100000 (not_8_out[1], Funct[5], ~Funct[4], ~Funct[3], ~Funct[2], ~Funct[1], ~Funct[0]);  // AND_Gate
  and _100010 (not_11_out[2], Funct[5], ~Funct[4], ~Funct[3], ~Funct[2], Funct[1], ~Funct[0]);  // AND_Gate
  and _100100 (_100100_out[3], Funct[5], ~Funct[4], ~Funct[3], Funct[2], ~Funct[1], ~Funct[0]);  // AND_Gate
  and _100101 (not_5_out[0], Funct[5], ~Funct[4], ~Funct[3], Funct[2], ~Funct[1], Funct[0]);  // AND_Gate
  and _100110 (not_13_out[1], Funct[5], ~Funct[4], ~Funct[3], Funct[2], Funct[1], ~Funct[0]);  // AND_Gate
  and _100111 (not_15_out[3], Funct[5], ~Funct[4], ~Funct[3], Funct[2], Funct[1], Funct[0]);  // AND_Gate
  and _101010 (not_17_out[2], Funct[5], ~Funct[4], Funct[3], ~Funct[2], Funct[1], ~Funct[0]);  // AND_Gate
  and _000000 (not_18_out[2], ~Funct[5], ~Funct[4], ~Funct[3], ~Funct[2], ~Funct[1], ~Funct[0]);  // AND_Gate
  and _000010 (not_21_out[2], ~Funct[5], ~Funct[4], ~Funct[3], ~Funct[2], Funct[1], ~Funct[0]);  // AND_Gate
  and _001000 (Jump_Register, ~Funct[5], ~Funct[4], Funct[3], ~Funct[2], ~Funct[1], ~Funct[0]);  // AND_Gate
  not not_1 (not_1_out[0], _100100_out[3]);
  not not_2 (not_1_out[1], _100100_out[3]);
  not not_3 (not_1_out[2], _100100_out[3]);
  not not_4 (not_1_out[3], _100100_out[3]);
  not not_5 (not_5_out[1], not_5_out[0]);
  not not_6 (not_5_out[2], not_5_out[0]);
  not not_7 (not_5_out[3], not_5_out[0]);
  not not_8 (not_8_out[0], not_8_out[1]);
  not not_9 (not_8_out[2], not_8_out[1]);
  not not_10 (not_8_out[3], not_8_out[1]);
  not not_11 (not_11_out[0], not_11_out[2]);
  not not_12 (not_11_out[3], not_11_out[2]);
  not not_13 (not_13_out[2], not_13_out[1]);
  not not_14 (not_13_out[3], not_13_out[1]);
  not not_15 (not_15_out[0], not_15_out[3]);
  not not_16 (not_15_out[1], not_15_out[3]);
  not not_17 (not_17_out[3], not_17_out[2]);
  not not_18 (not_18_out[0], not_18_out[2]);
  not not_19 (not_18_out[1], not_18_out[2]);
  not not_20 (not_18_out[3], not_18_out[2]);
  not not_21 (not_21_out[1], not_21_out[2]);
  not not_22 (not_21_out[3], not_21_out[2]);
  assign ADD_out = not_8_out & {4{not_8_out[1]}};  // AND_Gate ADD, 4 bits wide
  assign SUB_out = {not_11_out[3:2], not_11_out[2], not_11_out[0]} & {4{not_11_out[2]}};  // AND_Gate SUB, 4 bits wide
  assign AND_out = not_1_out & {4{_100100_out[3]}};  // AND_Gate AND, 4 bits wide
  assign OR_out = not_5_out & {4{not_5_out[0]}};  // AND_Gate OR, 4 bits wide
  assign XOR_out = {not_13_out, not_13_out[1]} & {4{not_13_out[1]}};  // AND_Gate XOR, 4 bits wide
  assign NOR_out = {{2{not_15_out[3]}}, not_15_out[1:0]} & {4{not_15_out[3]}};  // AND_Gate NOR, 4 bits wide
  assign SLT_out = {not_17_out, {2{not_17_out[2]}}} & {4{not_17_out[2]}};  // AND_Gate SLT, 4 bits wide
  assign SLL_out = not_18_out & {4{not_18_out[2]}};  // AND_Gate SLL, 4 bits wide
  assign SRL_out = {not_21_out, not_21_out[2]} & {4{not_21_out[2]}};  // AND_Gate SRL, 4 bits wide
  assign or_2_out = ADD_out | SUB_out | AND_out | OR_out | XOR_out | NOR_out | SLT_out | SLL_out | SRL_out;  // OR_Gate or_2, 4 bits wide
  Multiplexer #(.select(2), .width(4), .enable("false")) multiplexer_1 (
    .in0(or_2_out), .in1(4'b0010), .in2(4'b0110), .in3(4'b0001), .out(OP), .sel(ALUOP));

  // Notes on the sheet:
  //   AND 0000
  //   OR 0001
  //   ADD 0010
  //   XOR 0011
  //   SLL 0100
  //   SRL 0101
  //   SUB 0110
  //   SLT 0111
  //   NOR 1100
endmodule

module UCE (
  input  clock,
  input  Except,
  input  WriteRes,
  input  [31:0] EPC_in,
  input  [4:0] WR_in,
  input  [31:0] ResData,
  output [31:0] EPC,
  output [4:0] WR_out,
  output [31:0] MFC0_out
);

  Register #(.width(32)) u_EPC (.D(EPC_in), .en(Except), .Q(EPC), .clk(clock));  // open: clr
  Register #(.width(5)) WR (.D(WR_in), .en(Except), .Q(WR_out), .clk(clock));  // open: clr
  Register #(.width(32)) Res (.D(ResData), .en(WriteRes), .Q(MFC0_out), .clk(clock));  // open: clr
endmodule
