// Logisim project Datapath Main Circuit.circ as structural Verilog: 2 circuits, main circuit Esqueleto MIPS
module Esqueleto_MIPS (
  input  Clear
);

  wire add_0, ALUSrc, and_1_out, Bne, Branch, clock_1_out, Exception, ExcOut, Jump, JumpRegister, Link, lui,
       MemRead, MemtoReg, MemWrite, MFC0, MTC0, multiplexer_6_out, not_1_out, or_1_out, or_2_out, RegDst,
       Unsigned, WriteReg, zero;
  wire [1:0] uc_1_aluop;
  wire [3:0] Op;
  wire [4:0] multiplexer_9_out, multiplexer_10_out, multiplexer_16_out, rd, rs, rt, shamt, WR, WR_Except;
  wire [5:0] Funct, OpCode;
  wire [15:0] imm;
  wire [25:0] addr;
  wire [31:0] adder_1_out, datamemory_1_ld, EPC, imm32, inst, LD1, LD2, mfc0R, multiplexer_1_out,
       multiplexer_2_out, multiplexer_3_out, multiplexer_4_out, multiplexer_5_out, multiplexer_7_out,
       multiplexer_8_out, multiplexer_12_out, multiplexer_13_out, multiplexer_14_out, multiplexer_15_out,
       n2_conc_1_conc, PC___4, PCA, result;

  Multiplexer #(.width(32), .enable("false")) multiplexer_1 (
    .in0(multiplexer_2_out), .in1(n2_conc_1_conc), .out(multiplexer_1_out), .sel(Jump));
  // Probe on OpCode
  // Probe on rs
  // Probe on rt
  // Probe on shamt
  // Probe on Funct
  // Probe on imm
  // Probe on imm32
  // Probe on addr
  Multiplexer #(.width(32), .enable("false")) multiplexer_2 (
    .in0(multiplexer_5_out), .in1(LD1), .out(multiplexer_2_out), .sel(JumpRegister));
  Multiplexer #(.width(32), .enable("false")) multiplexer_3 (
    .in0(multiplexer_1_out), .in1(32'h4000000), .out(multiplexer_3_out), .sel(Exception));
  // Probe on inst
  // Probe on PCA
  // Probe on LD2
  Multiplexer #(.width(32), .enable("false")) multiplexer_4 (
    .in0(multiplexer_3_out), .in1(EPC), .out(multiplexer_4_out), .sel(ExcOut));
  // Probe on LD1
  // Probe on result
  // Probe on mfc0R
  // Probe on EPC
  // Probe on WR_Except
  Multiplexer #(.width(32), .enable("false")) multiplexer_5 (
    .in0(PC___4), .in1(adder_1_out), .out(multiplexer_5_out), .sel(and_1_out));
  Multiplexer #(.enable("false")) multiplexer_6 (.in0(zero), .in1(not_1_out), .out(multiplexer_6_out), .sel(Bne));
  not not_1 (not_1_out, zero);
  and and_1 (and_1_out, multiplexer_6_out, Branch);
  Multiplexer #(.width(32), .enable("false")) multiplexer_7 (
    .in0(multiplexer_4_out), .in1(32'h3ffffc), .out(multiplexer_7_out), .sel(add_0));
  Comparator #(.width(32)) comparator_1 (.a({32{1'b0}}), .b(PCA), .eq(add_0));  // open: gt, lt
  Clock clock_1 (.out(clock_1_out));
  Register #(.width(32)) PC (.D(multiplexer_7_out), .en(1'b1), .Q(PCA), .clk(clock_1_out), .clr(Clear));
  _2___conc u_2_conc_1 (.Conc(n2_conc_1_conc), .addr(addr), .PC___4(PC___4));
  Adder #(.width(32)) adder_1 (.a({imm32[29:0], 2'b00}), .b(PC___4), .out(adder_1_out));  // open: cin, cout
  Adder #(.width(32)) adder_2 (.a(32'h4), .b(PCA), .out(PC___4));  // open: cin, cout
  InstructionMem instructionmem_1 (.PcAddress(PCA), .Instruction(inst));
  Decoder decoder_1 (
    .instr(inst), .Funct(Funct), .RT(rt), .SHAMT(shamt), .RD(rd), .RS(rs), .IMM(imm), .Opcode(OpCode),
    .ADDR(addr));
  UC uc_1 (
    .Opcode(OpCode), .RegDst(RegDst), .WriteReg(WriteReg), .AluSrc(ALUSrc), .MemToReg(MemtoReg),
    .ExcOut(ExcOut), .MTC0(MTC0), .AluOp(uc_1_aluop), .MemRead(MemRead), .MemWrite(MemWrite),
    .Branch(Branch), .Jump(Jump), .Link(Link), .Bne(Bne), .MFC0(MFC0), .lui(lui), .\unsigned (Unsigned));
  Multiplexer #(.width(32), .enable("false")) multiplexer_8 (
    .in0(result), .in1(LD1), .out(multiplexer_8_out), .sel(MTC0));
  Multiplexer #(.width(5), .enable("false")) multiplexer_9 (.in0(rt), .in1(rd), .out(multiplexer_9_out), .sel(RegDst));
  or or_1 (or_1_out, MTC0, Exception);
  Extensor_de_sinal extensor_de_sinal_1 (.\input (imm), .\output (imm32), .Unsigned(Unsigned));
  Multiplexer #(.width(5), .enable("false")) multiplexer_10 (
    .in0(multiplexer_9_out), .in1(WR_Except), .out(multiplexer_10_out), .sel(ExcOut));
  UCE uce_1 (
    .EPC_in(PC___4), .WR_in(WR), .ResData(multiplexer_8_out), .EPC(EPC), .WR_out(WR_Except),
    .MFC0_out(mfc0R), .clock(clock_1_out), .Except(Exception), .WriteRes(or_1_out));
  Multiplexer #(.width(5), .enable("false")) multiplexer_11 (
    .in0(multiplexer_10_out), .in1({5{1'b1}}), .out(WR), .sel(Link));
  Multiplexer #(.width(32), .enable("false")) multiplexer_12 (
    .in0(multiplexer_14_out), .in1(mfc0R), .out(multiplexer_12_out), .sel(or_2_out));
  or or_2 (or_2_out, MFC0, ExcOut);
  ALUControl alucontrol_1 (.Funct(Funct), .ALUOP(uc_1_aluop), .OP(Op), .Jump_Register(JumpRegister));
  Multiplexer #(.width(32), .enable("false")) multiplexer_13 (
    .in0(multiplexer_12_out), .in1(PC___4), .out(multiplexer_13_out), .sel(Link));
  Banco_de_Registradores_de_32_bits banco_de_registradores_de_32_bits_1 (
    .RegWrite(WriteReg), .WR(WR), .WD(multiplexer_13_out), .LR1(rs), .LD1(LD1), .LR2(rt), .LD2(LD2),
    .Clock(clock_1_out), .Clear(Clear));
  Multiplexer #(.width(32), .enable("false")) multiplexer_14 (
    .in0(result), .in1(datamemory_1_ld), .out(multiplexer_14_out), .sel(MemtoReg));
  Multiplexer #(.width(32), .enable("false")) multiplexer_15 (
    .in0(LD2), .in1(imm32), .out(multiplexer_15_out), .sel(ALUSrc));
  Multiplexer #(.width(5), .enable("false")) multiplexer_16 (
    .in0(shamt), .in1(5'b10000), .out(multiplexer_16_out), .sel(lui));
  ULA ula_1 (
    .A(LD1), .B(multiplexer_15_out), .Result(result), .OP(Op), .Shamt(multiplexer_16_out), .Zero(zero),
    .Overflow(Exception));
  DataMemory datamemory_1 (
    .MemWrite(MemWrite), .MemRead(MemRead), .EL(result), .WD(LD2), .clock(clock_1_out), .LD(datamemory_1_ld),
    .clear(Clear));
endmodule

module _2___conc (
  input  [31:0] PC___4,
  input  [25:0] addr,
  output [31:0] Conc
);


  assign Conc = {PC___4[31:28], addr, 2'b00};
endmodule
