// Logisim project Decoder and Signal Extender.circ as structural Verilog: 2 circuits, main circuit Decoder
module Decoder (
  input  [31:0] instr,
  output [5:0] Funct,
  output [4:0] RT,
  output [4:0] SHAMT,
  output [4:0] RD,
  output [4:0] RS,
  output [15:0] IMM,
  output [5:0] Opcode,
  output [25:0] ADDR
);

  wire and_1_out, J_out, Jal_out, or_1_out;
  wire [25:0] \Não_é_R ;
  wire [25:16] I, R;

  Demultiplexer #(.width(26), .enable("false")) demultiplexer_1 (
    .out0(\Não_é_R ), .out1({R, RD, SHAMT, Funct}), .in(instr[25:0]), .sel(and_1_out));
  and and_1 (and_1_out, ~instr[26], ~instr[27], ~instr[28], ~instr[29], ~instr[30], ~instr[31]);  // AND_Gate
  and J (J_out, ~instr[31], ~instr[30], ~instr[29], ~instr[28], instr[27], ~instr[26]);  // AND_Gate
  and Jal (Jal_out, ~instr[31], ~instr[30], ~instr[29], ~instr[28], instr[27], instr[26]);  // AND_Gate
  or or_1 (or_1_out, J_out, Jal_out);
  Demultiplexer #(.width(26), .enable("false")) demultiplexer_2 (
    .out0({I, IMM}), .out1(ADDR), .in(\Não_é_R ), .sel(or_1_out));
  assign RT = R[20:16] | I[20:16];  // OR_Gate or_2, 5 bits wide
  assign RS = R[25:21] | I[25:21];  // OR_Gate or_3, 5 bits wide

  assign Opcode = instr[31:26];

  // Other names for the same wires on the sheet: I[15:0] = IMM; J[25:0] = ADDR; R[15:0] = {RD, SHAMT, Funct};
  //   RSI[4:0] = I[25:21]; RSR[4:0] = R[25:21]; RTI[4:0] = I[20:16]; RTR[4:0] = R[20:16]
endmodule

module Extensor_de_sinal (
  input  [15:0] \input ,
  input  Unsigned,
  output [31:0] \output 
);

  Multiplexer #(.enable("false")) multiplexer_1 (.in0(\input [15]), .in1(1'b0), .out(\output [31]), .sel(Unsigned));

  assign \output [30:0] = {{15{\output [31]}}, \input };
endmodule
