// Logisim project Memories.circ as structural Verilog: 3 circuits, main circuit decoder
module decoder (
  input  [31:0] Instr,
  input  [15:0] Imm,
  input  [25:0] addr,
  output [5:0] Opcode,
  output [5:0] Funct,
  output [4:0] Shamt,
  output [4:0] rd,
  output [4:0] rt,
  output [4:0] rs
);

  wire J_out, JAL_out, or_1_out, R_out;
  wire [25:0] J, Not_R_J, NotR;

  Demultiplexer #(.width(26), .tristate("true"), .enable("false")) demultiplexer_1 (
    .out0(NotR), .out1({rs, rt, rd, Shamt, Funct}), .in(Instr[25:0]), .sel(R_out));
  and R (R_out, ~Instr[31], ~Instr[30], ~Instr[29], ~Instr[28], ~Instr[27], ~Instr[26]);  // AND_Gate
  and u_J (J_out, ~Instr[31], ~Instr[30], ~Instr[29], ~Instr[28], Instr[27], ~Instr[26]);  // AND_Gate
  or or_1 (or_1_out, J_out, JAL_out);
  Demultiplexer #(.width(26), .tristate("true"), .enable("false")) demultiplexer_2 (
    .out0(Not_R_J), .out1(J), .in(NotR), .sel(or_1_out));
  and JAL (JAL_out, ~Instr[31], ~Instr[30], ~Instr[29], ~Instr[28], Instr[27], Instr[26]);  // AND_Gate

  assign Opcode = Instr[31:26];

  // Other names for the same wires on the sheet: R[25:0] = {rs, rt, rd, Shamt, Funct}
endmodule

module InstructionMem (
  input  [31:0] PcAddress,
  output [31:0] Instruction
);

  wire not_1_out, or_1_out;

  // Probe on PcAddress
  or or_1 (or_1_out, PcAddress[26], PcAddress[27], PcAddress[28], PcAddress[29], PcAddress[30], PcAddress[31]);
  not not_1 (not_1_out, or_1_out);
  ROM #(.addrWidth(24), .dataWidth(32)) rom_1 (.addr(PcAddress[25:2]), .data(Instruction), .sel(not_1_out));
  ROM #(.addrWidth(24), .dataWidth(32)) rom_2 (.addr(PcAddress[25:2]), .data(Instruction), .sel(or_1_out));

  // Notes on the sheet:
  //   contents of rom_1 (hex, n*v repeats v):
  //   0 12345
  //   contents of rom_2 (hex, n*v repeats v):
  //   0 234112
endmodule

module DataMemory (
  input  MemWrite,
  input  MemRead,
  input  [31:0] EL,
  input  [31:0] WD,
  input  clock,
  input  clear,
  output [31:0] LD
);

  wire not_1_out, or_1_out;

  or or_1 (or_1_out, EL[26], EL[27], EL[28], EL[29], EL[30], EL[31]);
  not not_1 (not_1_out, or_1_out);
  RAM #(.addrWidth(24), .dataWidth(32), .bus("separate")) ram_1 (
    .addr(EL[25:2]), .din(WD), .data(LD), .str(MemWrite), .sel(not_1_out), .clk(clock), .ld(MemRead),
    .clr(clear));
  RAM #(.addrWidth(24), .dataWidth(32), .bus("separate")) ram_2 (
    .addr(EL[25:2]), .din(WD), .data(LD), .str(MemWrite), .sel(or_1_out), .clk(clock), .ld(MemRead),
    .clr(clear));
endmodule
